// Logisim project IT012_Lab02_25520280.circ as structural Verilog
module FA (
  input  A,
  input  B,
  input  Cin,
  output S,
  output Cout
);

  wire and_1_out, and_2_out, xor_1_out;

  xor xor_1 (xor_1_out, A, B);
  xor xor_2 (S, xor_1_out, Cin);
  and and_1 (and_1_out, A, B);
  and and_2 (and_2_out, xor_1_out, Cin);
  or or_1 (Cout, and_1_out, and_2_out);
endmodule

module ADDSUB4 (
  input  [3:0] A,
  input  [3:0] B,
  input  SUB,
  output V,
  output Z,
  output N,
  output [3:0] S,
  output C
);

  wire B_0_out, B_1_out, B_2_out, B_3_out, fa_1_cout, fa_2_cout, fa_3_cout, xor_1_out, xor_2_out;

  FA fa_1 (.A(A[0]), .B(B_0_out), .Cin(SUB), .S(S[0]), .Cout(fa_1_cout));
  // Probe on fa_1_cout
  xor B_0 (B_0_out, B[0], SUB);
  FA fa_2 (.A(A[1]), .B(B_1_out), .Cin(fa_1_cout), .S(S[1]), .Cout(fa_2_cout));
  xor B_1 (B_1_out, B[1], SUB);
  // Probe on fa_2_cout
  xor B_2 (B_2_out, B[2], SUB);
  FA fa_3 (.A(A[2]), .B(B_2_out), .Cin(fa_2_cout), .S(S[2]), .Cout(fa_3_cout));
  // Probe on fa_3_cout
  xor B_3 (B_3_out, B[3], SUB);
  FA fa_4 (.A(A[3]), .B(B_3_out), .Cin(fa_3_cout), .S(N), .Cout(C));
  xor xor_1 (xor_1_out, A[3], N);
  xor xor_2 (xor_2_out, B_3_out, N);
  nor nor_1 (Z, S[0], S[1], S[2], N);
  and and_1 (V, xor_1_out, xor_2_out);

  assign S[3] = N;
endmodule

module REGFILE (
  input  WE,
  input  [1:0] RD,
  input  [1:0] RA,
  input  [7:0] DIN,
  input  CLK,
  input  [1:0] RB,
  output [7:0] R0,
  output [7:0] R1,
  output [7:0] R2,
  output [7:0] R3,
  output [7:0] QA,
  output [7:0] QB
);

  wire decoder_1_out0, decoder_1_out1, decoder_1_out2, decoder_1_out3;

  Decoder #(.select(2)) decoder_1 (
    .out0(decoder_1_out0), .out1(decoder_1_out1), .out2(decoder_1_out2), .out3(decoder_1_out3), .sel(RD),
    .en(WE));
  Register register_1 (.D(DIN), .en(decoder_1_out0), .Q(R0), .clk(CLK));  // open: clr
  Register register_2 (.D(DIN), .en(decoder_1_out1), .Q(R1), .clk(CLK));  // open: clr
  Register register_3 (.D(DIN), .en(decoder_1_out2), .Q(R2), .clk(CLK));  // open: clr
  Register register_4 (.D(DIN), .en(decoder_1_out3), .Q(R3), .clk(CLK));  // open: clr
  Multiplexer #(.select(2), .width(8), .enable("false")) multiplexer_1 (
    .in0(R0), .in1(R1), .in2(R2), .in3(R3), .out(QA), .sel(RA));
  Multiplexer #(.select(2), .width(8), .enable("false")) multiplexer_2 (
    .in0(R0), .in1(R1), .in2(R2), .in3(R3), .out(QB), .sel(RB));
endmodule

module ALU8 (
  input  [7:0] A,
  input  [7:0] B,
  input  [2:0] OP,
  output LT,
  output [7:0] AU_Out,
  output Z,
  output [7:0] R,
  output [7:0] LU_Out
);

  wire and_2_out, and_3_out, and_4_out, not_2_out;
  wire [7:0] adder_1_out, adder_2_out, and_1_out, not_1_out, or_1_out, subtractor_1_out, subtractor_2_out,
       xor_1_out;

  Adder adder_1 (.a(A), .b(B), .out(adder_1_out));  // open: cin, cout
  Adder adder_2 (.a(A), .b(8'h1), .out(adder_2_out));  // open: cin, cout
  Subtractor subtractor_1 (.a(A), .b(B), .out(subtractor_1_out));  // open: bin, bout
  Subtractor subtractor_2 (.a(A), .b(8'h1), .out(subtractor_2_out));  // open: bin, bout
  assign and_1_out = A & B;  // AND_Gate and_1, 8 bits wide
  assign or_1_out = A | B;  // OR_Gate or_1, 8 bits wide
  assign not_1_out = ~A;  // NOT_Gate not_1, 8 bits wide
  assign xor_1_out = A ^ B;  // XOR_Gate xor_1, 8 bits wide
  Multiplexer #(.select(2), .width(8), .enable("false")) multiplexer_1 (
    .in0(adder_1_out), .in1(adder_2_out), .in2(subtractor_1_out), .in3(subtractor_2_out), .out(AU_Out),
    .sel(OP[1:0]));
  Multiplexer #(.select(2), .width(8), .enable("false")) multiplexer_2 (
    .in0(and_1_out), .in1(or_1_out), .in2(not_1_out), .in3(xor_1_out), .out(LU_Out), .sel(OP[1:0]));
  Multiplexer #(.width(8), .enable("false")) multiplexer_3 (.in0(AU_Out), .in1(LU_Out), .out(R), .sel(OP[2]));
  not not_2 (not_2_out, B[7]);
  nor nor_1 (Z, R[0], R[1], R[2], R[3], R[4], R[5], R[6], R[7]);
  and and_2 (and_2_out, A[7], B[7]);
  and and_3 (and_3_out, A[7], not_2_out);
  and and_4 (and_4_out, B[7], subtractor_1_out[7]);
  or or_2 (LT, and_2_out, and_3_out, and_4_out);
endmodule

module DLATCH (
  input  D,
  input  E,
  output Q
);

  Multiplexer #(.enable("false")) multiplexer_1 (.in0(Q), .in1(D), .out(Q), .sel(E));
endmodule

module DFF_MS (
  input  D,
  input  CLK,
  output Q
);

  wire LATCH1_q, not_1_out;

  not not_1 (not_1_out, CLK);
  DLATCH LATCH1 (.D(D), .E(not_1_out), .Q(LATCH1_q));
  DLATCH LATCH2 (.D(LATCH1_q), .E(CLK), .Q(Q));
endmodule

module TN3 (
  input  D,
  input  CLK,
  output Q1,
  output Q2,
  output Q3
);

  DLATCH dlatch_1 (.D(D), .E(CLK), .Q(Q1));
  D_Flip_Flop d_ff_1 (.clk(CLK), .D(D), .Q(Q2));  // open: Qn, preset, en, reset
  DFF_MS dff_ms_1 (.D(D), .CLK(CLK), .Q(Q3));
endmodule

module DATAPATH (
  input  [1:0] RA,
  input  [1:0] RD,
  input  WE,
  input  [2:0] OP,
  input  [1:0] RB,
  input  SRC,
  input  [7:0] IMM,
  input  CLK,
  output [7:0] R,
  output Z,
  output [7:0] R0,
  output [7:0] R1,
  output [7:0] R2,
  output [7:0] R3
);

  wire [7:0] multiplexer_1_out, regfile_1_qa, regfile_1_qb;

  ALU8 alu8_1 (.A(regfile_1_qa), .B(regfile_1_qb), .OP(OP), .Z(Z), .R(R));  // open: LT, AU_Out, LU_Out
  Multiplexer #(.width(8), .enable("false")) multiplexer_1 (.in0(R), .in1(IMM), .out(multiplexer_1_out), .sel(SRC));
  REGFILE regfile_1 (
    .WE(WE), .RD(RD), .RA(RA), .DIN(multiplexer_1_out), .CLK(CLK), .RB(RB), .R0(R0), .R1(R1), .R2(R2),
    .R3(R3), .QA(regfile_1_qa), .QB(regfile_1_qb));
endmodule
