// Logisim project IT012_Lab02_25520280_TN1.circ as structural Verilog
module FA (
  input  A,
  input  B,
  input  Cin,
  output S,
  output Cout
);

  wire and_1_out, and_2_out, xor_1_out;

  xor xor_1 (xor_1_out, A, B);
  xor xor_2 (S, xor_1_out, Cin);
  and and_1 (and_1_out, A, B);
  and and_2 (and_2_out, xor_1_out, Cin);
  or or_1 (Cout, and_1_out, and_2_out);
endmodule

module ADDSUB4 (
  input  [3:0] A,
  input  [3:0] B,
  input  SUB,
  output V,
  output Z,
  output N,
  output [3:0] S,
  output C
);

  wire B_0_out, B_1_out, B_2_out, B_3_out, fa_1_cout, fa_2_cout, fa_3_cout, xor_1_out, xor_2_out;

  FA fa_1 (.A(A[0]), .B(B_0_out), .Cin(SUB), .S(S[0]), .Cout(fa_1_cout));
  // Probe on fa_1_cout
  xor B_0 (B_0_out, B[0], SUB);
  FA fa_2 (.A(A[1]), .B(B_1_out), .Cin(fa_1_cout), .S(S[1]), .Cout(fa_2_cout));
  xor B_1 (B_1_out, B[1], SUB);
  // Probe on fa_2_cout
  xor B_2 (B_2_out, B[2], SUB);
  FA fa_3 (.A(A[2]), .B(B_2_out), .Cin(fa_2_cout), .S(S[2]), .Cout(fa_3_cout));
  // Probe on fa_3_cout
  xor B_3 (B_3_out, B[3], SUB);
  FA fa_4 (.A(A[3]), .B(B_3_out), .Cin(fa_3_cout), .S(N), .Cout(C));
  xor xor_1 (xor_1_out, A[3], N);
  xor xor_2 (xor_2_out, B_3_out, N);
  nor nor_1 (Z, S[0], S[1], S[2], N);
  and and_1 (V, xor_1_out, xor_2_out);

  assign S[3] = N;
endmodule
